# Fritzing sketch Part A (saved by Fritzing 0.9.4)
breadboards: 1

parts:
  U1 = 7400 4 x 2 Input NAND Gate [part_number=7400 package="DIP (Dual Inline) [THT]"]
  Input_B = Header 1 [package=snap-male]
  Input_A = Header 1 [package=snap-male]
  Input_C = Header 1 [package=snap-male]
  Output_Z = Header 1 [package=snap-male]

nets:
  N1: U1.A1, U1.Q4
  N2: U1.B1, U1.B2
  N3: U1.Q1, Output_Z.1
  N4: U1.Q2, U1.A3
  N5: U1.A2, Input_C.1
  GND: U1.GND
  N6: U1.B3, U1.Q3, U1.A4, Input_B.1
  N7: U1.B4, Input_A.1

notes:
  Input B
  Output Z
  Input C
  Input A
