# Fritzing sketch Part B (saved by Fritzing 0.9.4)
breadboards: 1

parts:
  U1 = 7400 4 x 2 Input NAND Gate [part_number=7400 package="DIP (Dual Inline) [THT]"]
  Input_B = Header 1 [package=snap-male]
  Input_A = Header 1 [package=snap-male]
  Input_C = Header 1 [package=snap-male]
  Output_Z = Header 1 [package=snap-male]
  U2 = 7400 4 x 2 Input NAND Gate [part_number=7400 package="DIP (Dual Inline) [THT]"]

nets:
  N1: U1.A1, U1.Q4
  N2: U1.B1, U1.B2
  N3: U1.Q1, U2.A1, U2.B1
  N4: U1.Q2, U1.A3
  N5: U1.A2, Input_C.1, U2.A4
  GND: U1.GND, U2.GND
  N6: U1.B3, U1.Q3, U1.A4, Input_B.1
  N7: U1.B4, Input_A.1, U2.B4
  VDD: U1.VDD, U2.VDD
  N8: Output_Z.1, U2.B2
  N9: U2.Q1, U2.Q2
  N10: U2.A2, U2.Q4

notes:
  Input B
  Output Z
  Input C
  Input A
